// Logisim project 1.goop.1.gop.circ as structural Verilog: 1 circuit, main circuit main
module main (
  input  Clock,
  input  I1,
  input  I0,
  input  Data,
  output DBUS,
  output RR,
  output Write,
  output Jump
);

  wire d_ff_1_qn, nand_1_out, nand_2_out, nor_1_out, nor_2_out, nor_3_out, nor_4_out, nor_5_out, nor_6_out,
       nor_7_out, nor_8_out, nor_10_out, not_1_out, not_2_out, not_3_out;

  not not_1 (not_1_out, I1);
  not not_2 (not_2_out, I0);
  not not_3 (not_3_out, Data);
  nor nor_1 (nor_1_out, I0, Data);
  nor nor_2 (nor_2_out, I1, not_2_out, RR);
  nor nor_3 (nor_3_out, not_1_out, I0, d_ff_1_qn, not_3_out);
  nor nor_4 (nor_4_out, not_1_out, I0, Data);
  nor nor_5 (nor_5_out, I1, RR);
  nor nor_6 (nor_6_out, not_1_out, I0);
  nor nor_7 (nor_7_out, not_1_out, not_2_out, RR);
  nor nor_8 (nor_8_out, nor_3_out, nor_4_out, nor_5_out);
  nor nor_9 (DBUS, nor_1_out, nor_2_out, nor_4_out);
  D_Flip_Flop d_ff_1 (.D(nor_8_out), .clk(nor_10_out), .Q(RR), .Qn(d_ff_1_qn));  // open: preset, reset
  nor nor_10 (nor_10_out, Clock, nor_6_out, nor_7_out);
  nand nand_1 (nand_1_out, Clock, nor_6_out);
  nand nand_2 (nand_2_out, Clock, nor_7_out);
  not not_4 (Write, nand_1_out);
  not not_5 (Jump, nand_2_out);

  // Notes on the sheet:
  //   00: LD
  //   01: NOR
  //   10: STO
  //   11: JMP
  //   !i1&!i0&D
  //   i1&RR
  //   i1&!i0
  //   i0&D
  //   i1&!i0&RR
  //   !i1&i0&!RR&!D
  //   i1&i0&!RR
  //   RR out
  //   Write enable
  //   Jump enable
endmodule
