// Logisim project 1.goop.1.gop_v2.circ as structural Verilog: 1 circuit, main circuit main
module main (
  input  Clock,
  input  Data,
  input  I1,
  input  I0,
  output DBUS,
  output RR,
  output Write,
  output Jump
);

  wire nand_1_out, nand_2_out, nand_3_out, nor_1_out, nor_2_out, nor_3_out, nor_4_out, nor_5_out, nor_6_out,
       nor_7_out, nor_8_out, nor_9_out, nor_10_out, nor_11_out, nor_12_out, nor_13_out, nor_15_out,
       not_1_out, not_2_out, not_3_out, not_4_out, not_5_out;

  not not_1 (not_1_out, I1);
  not not_2 (not_2_out, I0);
  not not_3 (not_3_out, nand_1_out);
  nand nand_1 (nand_1_out, RR, nor_1_out);
  or or_1 (DBUS, Data, not_3_out);
  not not_4 (not_4_out, DBUS);
  nor nor_1 (nor_1_out, not_1_out, I0);
  nor nor_2 (nor_2_out, not_1_out, I0, nor_15_out, DBUS);
  nor nor_3 (nor_3_out, I1, I0, not_4_out);
  nor nor_4 (nor_4_out, I1, RR);
  nor nor_5 (nor_5_out, not_1_out, not_2_out, RR);
  nor nor_6 (nor_6_out, nor_2_out, nor_3_out, nor_4_out);
  nor nor_7 (nor_7_out, Clock, nor_1_out, nor_5_out);
  nor nor_8 (nor_8_out, nor_6_out, nor_7_out);
  nor nor_9 (nor_9_out, nor_8_out, nor_7_out);
  not not_5 (not_5_out, nor_7_out);
  nand nand_2 (nand_2_out, Clock, nor_1_out);
  nand nand_3 (nand_3_out, Clock, nor_5_out);
  nor nor_10 (nor_10_out, nor_8_out, nor_11_out);
  nor nor_11 (nor_11_out, nor_10_out, nor_9_out);
  not not_6 (Write, nand_2_out);
  not not_7 (Jump, nand_3_out);
  nor nor_12 (nor_12_out, nor_10_out, not_5_out);
  nor nor_13 (nor_13_out, nor_12_out, not_5_out);
  nor nor_14 (RR, nor_12_out, nor_15_out);
  nor nor_15 (nor_15_out, RR, nor_13_out);

  // Notes on the sheet:
  //   00: LD
  //   dbus = data
  //   rr = dbus
  //   write = 0
  //   jump = 0
  //   01: NOR
  //   dbus = data
  //   rr = !(rr + dbus)
  //   write = 0
  //   jump = 0
  //   i1&!i0&RR
  //   i1&!i0
  //   !i1&i0&!RR&!D
  //   !i1&!i0&D
  //   i1&RR
  //   i1&i0&!RR
  //   10: STO
  //   write = 1
  //   jump = 0
  //   Write enable
  //   Jump enable
  //   dbus = rr
  //   rr = rr
  //   RR out
  //   11: JMP
  //   dbus = data
  //   rr = rr
  //   write = 0
  //   jump = 1
  //   NOR gate: one toggle, all others low
  //   AND gate: NOR with inverted inputs
endmodule
