// Logisim project gglu_v2.circ as structural Verilog: 1 circuit, main circuit main
module main (
  input  Clk,
  input  D,
  input  i1,
  input  i0,
  output Dbus,
  output RR,
  output W,
  output J,
  output dbus2,
  output rr2,
  output w2,
  output j2
);

  wire and_1_out, multiplexer_2_out, nor_1_out, nor_2_out, nor_3_out, nor_5_out, nor_6_out, nor_7_out,
       nor_8_out, nor_9_out, nor_12_out, nor_13_out, nor_14_out, nor_15_out, nor_16_out, nor_17_out,
       nor_19_out, not_1_out, not_2_out, not_3_out, not_4_out, not_5_out, not_6_out, not_7_out;

  Multiplexer multiplexer_1 (.in0(D), .in1(RR), .out(Dbus), .sel(i1));
  not not_1 (not_1_out, i1);
  not not_2 (not_2_out, i0);
  nor nor_1 (nor_1_out, Dbus, RR);
  nor nor_2 (nor_2_out, D, i1);
  nor nor_3 (nor_3_out, not_1_out, rr2);
  Multiplexer multiplexer_2 (.in0(Dbus), .in1(nor_1_out), .out(multiplexer_2_out), .sel(i0));
  nor nor_4 (dbus2, nor_2_out, nor_3_out);
  and and_1 (and_1_out, Clk, not_3_out);
  not not_3 (not_3_out, i1);
  not not_4 (not_4_out, i0);
  nor nor_5 (nor_5_out, dbus2, rr2);
  not not_5 (not_5_out, nor_5_out);
  D_Flip_Flop d_ff_1 (.D(multiplexer_2_out), .clk(and_1_out), .Q(RR));  // open: Qn, preset, reset
  and and_2 (W, i1, Clk, not_4_out);
  and and_3 (J, i1, Clk, i0, nor_1_out);
  nor nor_6 (nor_6_out, dbus2, i0);
  nor nor_7 (nor_7_out, not_2_out, nor_5_out);
  not not_6 (not_6_out, Clk);
  nor nor_8 (nor_8_out, nor_6_out, nor_7_out);
  nor nor_9 (nor_9_out, not_6_out, i1);
  nor nor_10 (w2, not_1_out, not_6_out, i0);
  nor nor_11 (j2, not_1_out, not_6_out, not_2_out, not_5_out);
  nor nor_12 (nor_12_out, nor_8_out, nor_9_out);
  nor nor_13 (nor_13_out, nor_12_out, nor_9_out);
  not not_7 (not_7_out, nor_9_out);
  nor nor_14 (nor_14_out, nor_12_out, nor_16_out);
  nor nor_15 (nor_15_out, nor_14_out, not_7_out);
  nor nor_16 (nor_16_out, nor_14_out, nor_13_out);
  nor nor_17 (nor_17_out, nor_15_out, not_7_out);
  nor nor_18 (rr2, nor_15_out, nor_19_out);
  nor nor_19 (nor_19_out, rr2, nor_17_out);

  // Other names for the same wires on the sheet: Clock = Clk; Data = D
endmodule
