// Logisim project gglu_v3.circ as structural Verilog: 1 circuit, main circuit main
module main (
  input  in_1,
  input  in_2,
  input  in_3,
  input  in_4,
  output out_5,
  output out_6,
  output out_7,
  output out_8
);

  wire nor_1_out, nor_2_out, nor_4_out, nor_5_out, nor_6_out, nor_7_out, nor_8_out, nor_11_out, nor_12_out,
       nor_13_out, nor_14_out, nor_16_out, not_1_out, not_2_out, not_3_out, not_4_out;

  not not_1 (not_1_out, in_3);
  not not_2 (not_2_out, in_4);
  nor nor_1 (nor_1_out, in_2, in_3);
  nor nor_2 (nor_2_out, not_1_out, out_6);
  nor nor_3 (out_5, nor_1_out, nor_2_out);
  nor nor_4 (nor_4_out, out_5, out_6);
  not not_3 (not_3_out, nor_4_out);
  nor nor_5 (nor_5_out, out_5, in_4);
  nor nor_6 (nor_6_out, not_2_out, nor_4_out);
  not not_4 (not_4_out, in_1);
  nor nor_7 (nor_7_out, nor_5_out, nor_6_out);
  nor nor_8 (nor_8_out, in_1, in_3);
  nor nor_9 (out_7, not_1_out, not_4_out, in_4);
  nor nor_10 (out_8, not_1_out, not_4_out, not_2_out, not_3_out);
  nor nor_11 (nor_11_out, nor_14_out, nor_12_out);
  nor nor_12 (nor_12_out, nor_11_out, nor_8_out);
  nor nor_13 (nor_13_out, nor_12_out, nor_8_out, nor_14_out);
  nor nor_14 (nor_14_out, nor_13_out, nor_7_out);
  nor nor_15 (out_6, nor_12_out, nor_16_out);
  nor nor_16 (nor_16_out, out_6, nor_13_out);

  // Other names for the same wires on the sheet: Clock = in_1; Data = in_2; Dbus = out_5; i0 = in_4; i1 = in_3;
  //   Jump = out_8; RR = out_6; Write = out_7

  // Notes on the sheet:
  //   !i0
  //   !i1
  //   !(D+i1)
  //   !(!i1+RR)
  //   !(!(D+i1)+!(!i1+RR))
  //   =(D+i1)&(!i1+RR)
endmodule
