// Logisim project latch_tests.circ as structural Verilog: 1 circuit, main circuit main
module main (
  input  in_1,
  input  in_2,
  output builtin_dff,
  output mux_dff,
  output sr_nor_dff,
  output nor_mux_dff
);

  wire multiplexer_1_out, nor_1_out, nor_2_out, nor_3_out, nor_4_out, nor_5_out, nor_6_out, nor_7_out,
       nor_8_out, nor_9_out, nor_10_out, nor_11_out, nor_13_out, not_1_out, not_2_out;

  not not_1 (not_1_out, in_1);
  Multiplexer multiplexer_1 (.in0(in_2), .in1(multiplexer_1_out), .out(multiplexer_1_out), .sel(in_1));
  not not_2 (not_2_out, in_1);
  nor nor_1 (nor_1_out, in_2, in_1);
  nor nor_2 (nor_2_out, nor_7_out, not_1_out);
  D_Flip_Flop d_ff_1 (.D(in_2), .clk(in_1), .Q(builtin_dff));  // open: Qn, preset, reset
  nor nor_3 (nor_3_out, in_2, in_1);
  nor nor_4 (nor_4_out, nor_3_out, in_1);
  Multiplexer multiplexer_2 (.in0(mux_dff), .in1(multiplexer_1_out), .out(mux_dff), .sel(in_1));
  nor nor_5 (nor_5_out, nor_3_out, nor_6_out);
  nor nor_6 (nor_6_out, nor_5_out, nor_4_out);
  nor nor_7 (nor_7_out, nor_1_out, nor_2_out);
  nor nor_8 (nor_8_out, nor_mux_dff, in_1);
  nor nor_9 (nor_9_out, nor_7_out, not_1_out);
  nor nor_10 (nor_10_out, nor_5_out, not_2_out);
  nor nor_11 (nor_11_out, nor_10_out, not_2_out);
  nor nor_12 (sr_nor_dff, nor_10_out, nor_13_out);
  nor nor_13 (nor_13_out, sr_nor_dff, nor_11_out);
  nor nor_14 (nor_mux_dff, nor_8_out, nor_9_out);

  // Other names for the same wires on the sheet: clk = in_1; data = in_2
endmodule
